# Fritzing sketch Spark Plug Detector (saved by Fritzing 0.9.4)
circuit board: 8.46667cm x 5.64444cm
breadboards: 1

parts:
  BC1 = CD4093 [part_number=CD4093BC package="DIP14 [THT]"]
  C3 = Ceramic Capacitor [capacitance=100nF package="100 mil [THT, multilayer]"]
  R3 = Resistor [tolerance=±5% resistance=27k package=THT]
  J1 = male pin header, 2 pins [form="♂ (male)"]
  J2 = male pin header, 2 pins [form="♂ (male)"]
  C2 = Ceramic Capacitor [capacitance=220pF package="100 mil [THT, multilayer]"]
  R1 = Resistor [tolerance=±5% resistance=4.7k package=THT]
  R2 = Resistor [tolerance=±5% resistance=39k package=THT]
  C4 = Ceramic Capacitor [capacitance=100nF package="100 mil [THT, multilayer]"]
  C1 = Film/Foil Capacitor [capacitance=100nF voltage=35V package="5mm [THT, pp]"]
  J5 = male pin header, 1 pin [form="♂ (male)"]
  J4 = male pin header, 1 pin [form="♂ (male)"]
  J3 = male pin header, 1 pin [form="♂ (male)"]

nets:
  N1: BC1.A, BC1.B, BC1.F, BC1.M
  N2: BC1.J, J4.pin1
  N3: BC1.C, BC1.D, BC1.GND, R3.Pin_1, J1.pin2, R2.Pin_1, C4.1, J3.pin1
  N4: BC1.E, R1.Pin_1
  N5: BC1.L, C3.1
  N6: BC1.G, C3.0, R3.Pin_0
  N7: BC1.H, BC1.VCC, C4.0, J5.pin1
  N8: J1.pin1, C1.-
  N9: J2.pin2, C2.1
  N10: C2.0, R1.Pin_0, R2.Pin_0, C1.+

notes:
  Test
  (5-12VAC)
  IN
  3.3 VDC
  OUT
  GND

custom parts:
  CD4093: Quad NAN Schmitt Trigger
